# Fritzing sketch timer (saved by Fritzing 0.9.2b)
breadboards: 1

parts:
  Raspberry_Pi1 = Raspberry Pi B rev2
  LED1 = smd LED [color="Red (633nm)" package="0603 [SMD]"]
  LED2 = smd LED [color="Green (565nm)" package="0603 [SMD]"]
  R1 = Resistor [tolerance=±5% resistance=200 package="1206 [SMD]"]
  R2 = Resistor [tolerance=±5% resistance=200 package="1206 [SMD]"]

nets:
  N1: Raspberry_Pi1.3V3, R1.Pin_0, R2.Pin_0
  N2: Raspberry_Pi1.GPIO_17, LED1.cathode
  N3: Raspberry_Pi1.GPIO_18, LED2.cathode
  N4: LED1.anode, R2.Pin_1
  N5: LED2.anode, R1.Pin_1
